// Logisim project MiniRISCV.circ as structural Verilog: 7 circuits, main circuit main
module main (
  input  in_1,
  input  [3:0] in_2,
  input  in_3,
  input  in_4,
  input  in_5,
  input  in_6
);

  wire clock_1_out, comparator_black_box_1_p3, comparator_black_box_1_p4, decode_black_box_1_p2,
       decode_black_box_1_p3, decode_black_box_1_p4, undriven, undriven_2, undriven_3, undriven_4, undriven_5;
  wire [3:0] decode_black_box_1_p6, multiplexer_3_out;
  wire [4:0] multiplexer_5_out, sa_1_out_2;
  wire [11:0] decode_black_box_1_p29;
  wire [21:0] decode_black_box_1_p7;
  wire [31:0] alu_1_p5, bit_extender_1_out, decode_black_box_1_p5, if_id_1_inst_o, if_id_1_pc_o,
       multiplexer_1_out, multiplexer_2_out, multiplexer_4_out, pc_1_pc, pc_1_pc_4, registerfile_1_p1,
       registerfile_1_p7, registerfile_1_p8, risc_vprogramrom_1_p2;

  PC pc_1 (.we(in_5), .clk(clock_1_out), .clr(in_6), .PC_4(pc_1_pc_4), .PC(pc_1_pc));
  Clock clock_1 (.out(clock_1_out));
  // RISC_VProgramROM risc_vprogramrom_1: pin names not known; wires that end beside it: pc_1_pc, risc_vprogramrom_1_p2
  IF_ID if_id_1 (
    .inst(risc_vprogramrom_1_p2), .clk(clock_1_out), .PC4(pc_1_pc_4), .inst_o(if_id_1_inst_o),
    .PC_o(if_id_1_pc_o));
  // Decode_Black_Box decode_black_box_1: pin names not known; wires that end beside it: if_id_1_inst_o, decode_black_box_1_p2, decode_black_box_1_p3, decode_black_box_1_p4, decode_black_box_1_p5, decode_black_box_1_p6, decode_black_box_1_p7[0], decode_black_box_1_p7[1], decode_black_box_1_p7[2], decode_black_box_1_p7[3], decode_black_box_1_p7[4], decode_black_box_1_p7[5], decode_black_box_1_p7[6], decode_black_box_1_p7[7], decode_black_box_1_p7[8], decode_black_box_1_p7[9], decode_black_box_1_p7[10], decode_black_box_1_p7[11], decode_black_box_1_p7[12], decode_black_box_1_p7[13], decode_black_box_1_p7[14], decode_black_box_1_p7[15], decode_black_box_1_p7[16], decode_black_box_1_p7[17], decode_black_box_1_p7[18], decode_black_box_1_p7[19], decode_black_box_1_p7[20], decode_black_box_1_p7[21], decode_black_box_1_p29[0], decode_black_box_1_p29[1], decode_black_box_1_p29[2], decode_black_box_1_p29[3], decode_black_box_1_p29[4], decode_black_box_1_p29[5], decode_black_box_1_p29[6], decode_black_box_1_p29[7], decode_black_box_1_p29[8]
  // RegisterFile registerfile_1: pin names not known; wires that end beside it: registerfile_1_p1, clock_1_out, 1'b1, decode_black_box_1_p4, decode_black_box_1_p2, decode_black_box_1_p3, registerfile_1_p7, registerfile_1_p8
  ID_EX id_ex_1 (
    .inst(if_id_1_inst_o), .clk(clock_1_out), .PC_4(if_id_1_pc_o), .A(registerfile_1_p7),
    .B(registerfile_1_p8), .imm(decode_black_box_1_p5), .ctrl_A(decode_black_box_1_p7),
    .ctrl_B(decode_black_box_1_p29));  // open: inst_o, PC_o, A_o, B_o, imm_o, ctrl_A_o, ctrl_B_o
  Multiplexer #(.width(32), .enable("false")) multiplexer_1 (
    .in0(registerfile_1_p7), .in1(decode_black_box_1_p5), .out(multiplexer_1_out), .sel(undriven));
  Multiplexer #(.width(32), .enable("false")) multiplexer_2 (
    .in0(registerfile_1_p8), .in1(decode_black_box_1_p5), .out(multiplexer_2_out), .sel(undriven_2));
  Multiplexer #(.width(4), .enable("false")) multiplexer_3 (
    .in0(decode_black_box_1_p6), .in1(4'b0111), .out(multiplexer_3_out), .sel(undriven_4));
  Multiplexer #(.width(32), .enable("false")) multiplexer_4 (
    .in0(multiplexer_2_out), .in1(if_id_1_pc_o), .out(multiplexer_4_out), .sel(undriven_3));
  SA sa_1 (.SA_32(multiplexer_2_out), .out_2(sa_1_out_2));
  Multiplexer #(.width(5), .enable("false")) multiplexer_5 (
    .in0(sa_1_out_2), .in1(5'b01100), .out(multiplexer_5_out), .sel(undriven_4));
  // Comparator_Black_Box comparator_black_box_1: pin names not known; wires that end beside it: multiplexer_1_out, multiplexer_2_out, comparator_black_box_1_p3, comparator_black_box_1_p4
  // ALU alu_1: pin names not known; wires that end beside it: multiplexer_1_out, multiplexer_4_out, multiplexer_3_out, multiplexer_5_out, alu_1_p5
  assign bit_extender_1_out = {{31{comparator_black_box_1_p4}}, comparator_black_box_1_p4};  // Bit_Extender bit_extender_1
  Multiplexer #(.width(32), .enable("false")) multiplexer_6 (
    .in0(alu_1_p5), .in1(bit_extender_1_out), .out(registerfile_1_p1), .sel(undriven_5));
  // RAM ram_1: pin names not known; wires that end beside it: registerfile_1_p1, in_1, in_2, clock_1_out, in_3, in_4

  // Notes on the sheet:
  //   contents of risc_vprogramrom_1 (hex, n*v repeats v):
  //   lui t1, 1 lui t2, 2  add t3, t1, t0 # t2 = t1 +t0 xor t4, t1, t2 or t5, t1, t2 auipc a0, 0 sub t0,
  //   t1, t2 # t0 = t1 - t2
endmodule

module PC (
  input  we,
  input  clk,
  input  clr,
  output [31:0] PC_4,
  output [31:0] PC
);

  wire incrementer_1_p2, incrementer_2_p2, incrementer_3_p2;

  Register #(.width(32)) clk_in (.D(PC_4), .en(we), .clk(clk), .Q(PC), .clr(clr));
  // Incrementer #(.width(32)) incrementer_1: pin names not known; wires that end beside it: PC, incrementer_1_p2
  // Incrementer #(.width(32)) incrementer_2: pin names not known; wires that end beside it: incrementer_1_p2, incrementer_2_p2
  // Incrementer #(.width(32)) incrementer_3: pin names not known; wires that end beside it: incrementer_2_p2, incrementer_3_p2
  // Incrementer #(.width(32)) incrementer_4: pin names not known; wires that end beside it: incrementer_3_p2, PC_4
endmodule

module SA (
  input  [31:0] SA_32,
  output [4:0] out_2
);


  assign out_2 = SA_32[4:0];
endmodule

module IF_ID (
  input  [31:0] inst,
  input  clk,
  input  [31:0] PC4,
  output [31:0] inst_o,
  output [31:0] PC_o
);

  Register #(.width(32)) register_1 (.D(inst), .en(1'b1), .clk(clk), .Q(inst_o), .clr(1'b0));
  Register #(.width(32)) register_2 (.D(PC4), .en(1'b1), .clk(clk), .Q(PC_o), .clr(1'b0));
endmodule

module plus_4 (
  input  [31:0] p_in,
  output [31:0] out_2
);

  wire incrementer_1_p2, incrementer_2_p2, incrementer_3_p2;

  // Incrementer #(.width(32)) incrementer_1: pin names not known; wires that end beside it: p_in, incrementer_1_p2
  // Incrementer #(.width(32)) incrementer_2: pin names not known; wires that end beside it: incrementer_1_p2, incrementer_2_p2
  // Incrementer #(.width(32)) incrementer_3: pin names not known; wires that end beside it: incrementer_2_p2, incrementer_3_p2
  // Incrementer #(.width(32)) incrementer_4: pin names not known; wires that end beside it: incrementer_3_p2, out_2
endmodule

module PC_test (
  input  in_1,
  input  in_2,
  input  in_3,
  output [31:0] out_4
);

  wire undriven, undriven_2, undriven_3, undriven_4, undriven_5, undriven_6, undriven_7, undriven_8,
       undriven_9, undriven_10, undriven_11, undriven_12;

  Register #(.width(32)) register_1 (.D(out_4), .en(in_1), .clk(in_2), .Q(out_4), .clr(in_3));
  // OR_Gate or_1 has open pins: in0=undriven_9, in1=undriven_6, in2=undriven_5, in4=undriven_3, in5=undriven, in6=undriven_7, in7=undriven_8, in8=undriven_10, out=open
  // NOR_Gate nor_1 has open pins: in0=undriven_2, in1=undriven, out=open
  // OR_Gate or_2 has open pins: in0=undriven_4, in1=undriven_3, in2=undriven_2, in3=undriven, out=open
  // OR_Gate or_3 has open pins: in0=undriven_11, in1=undriven_12, out=open
endmodule

module ID_EX (
  input  [31:0] inst,
  input  clk,
  input  [31:0] PC_4,
  input  [31:0] A,
  input  [31:0] B,
  input  [31:0] imm,
  input  [21:0] ctrl_A,
  input  [11:0] ctrl_B,
  output [31:0] inst_o,
  output [31:0] PC_o,
  output [31:0] A_o,
  output [31:0] B_o,
  output [31:0] imm_o,
  output [21:0] ctrl_A_o,
  output [11:0] ctrl_B_o
);

  Register #(.width(32)) register_1 (.D(inst), .en(1'b1), .clk(clk), .Q(inst_o), .clr(1'b0));
  Register #(.width(32)) register_2 (.D(PC_4), .en(1'b1), .clk(clk), .Q(PC_o), .clr(1'b0));
  Register #(.width(32)) register_3 (.D(A), .en(1'b1), .clk(clk), .Q(A_o), .clr(1'b0));
  Register #(.width(32)) register_4 (.D(B), .en(1'b1), .clk(clk), .Q(B_o), .clr(1'b0));
  Register #(.width(32)) register_5 (.D(imm), .en(1'b1), .clk(clk), .Q(imm_o), .clr(1'b0));
  Register #(.width(22)) register_6 (.D(ctrl_A), .en(1'b1), .clk(clk), .Q(ctrl_A_o), .clr(1'b0));
  Register #(.width(12)) register_7 (.D(ctrl_B), .en(1'b1), .clk(clk), .Q(ctrl_B_o), .clr(1'b0));
endmodule
